# Fritzing sketch biotec_countdown_part_scheme (saved by Fritzing 0.9.6b)

parts:
  RASPBERRY_PICO_WH = Raspberry Pi Pico
  NEOXPIXEL_x60* = WS2812 RGB LED strip
  LED = smd LED [color="Green (560nm)" package="0603 [SMD]"]

nets:
  N1: RASPBERRY_PICO_WH.pin_1, NEOXPIXEL_x60*.DIN
  N2: RASPBERRY_PICO_WH.pin_8, RASPBERRY_PICO_WH.pin_38, RASPBERRY_PICO_WH.pin_42, NEOXPIXEL_x60*.GND, LED.cathode
  N3: RASPBERRY_PICO_WH.pin_10, LED.anode
  N4: RASPBERRY_PICO_WH.pin_40, NEOXPIXEL_x60*.VCC

custom parts:
  Raspberry Pi Pico: Raspberry Pi Pico. Based around the RP2040 microcontroller the Pico is a low cost microcontroller device bringing Raspberry Pi quality, cost, and easy of use to the microcontroller space. Jan 2021, Split part in to two versions: tht (this one) and SMD. This one will drill holes for a .1 in header in pcb to allow plugging in the module as well as providing pads to solder the module to the top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
  WS2812 RGB LED strip: WS2812 strip
