# Fritzing sketch Schema_fritzing_minitel (saved by Fritzing 0.9.6b)
breadboards: 1

parts:
  DIN1 = DIN-5 jack (MIDI) [package=THT]
  USBUART1 = CP2102 USB UART Breakout
  Raspberry_Pi_1 = Raspberry Pi 3 [part_number=RPI-3-V1.2]  # not connected
  Q1 = TRANSISTOR_NPN [part_number=2N2222A package=to-92]
  R1 = Resistor [tolerance=±5% resistance=220k package="2010 [SMD]"]
  R2 = Resistor [tolerance=±5% resistance=22k package="2010 [SMD]"]
  R3 = Resistor [tolerance=±5% resistance=10k package="2010 [SMD]"]

nets:
  N1: DIN1.3, USBUART1.TXD, R1.Pin_1
  N2: DIN1.2, USBUART1.GND, R2.Pin_1
  N3: DIN1.1, Q1.C
  N4: USBUART1.VCCIO, R1.Pin_0, R3.Pin_0
  N5: USBUART1.RXD, Q1.E
  N6: Q1.B, R2.Pin_0, R3.Pin_1

custom parts:
  CP2102 USB UART Breakout: CP2102 Usb Uart Breakout Board with Battery
