# Fritzing sketch Fake_Bomb_Escape (saved by Fritzing 0.9.6b)
breadboards: 1

parts:
  Composant2 = Arduino Uno (Rev3)
  LED1 = LED - 3mm [color="Red (633nm)" current=0.030 package="3 mm [THT]"]
  J1 = Piezo Speaker
  LED2 = LED - 3mm [color="Yellow (595nm)" current=0.030 package="3 mm [THT]"]
  LED3 = LED - 3mm [color="Green (555nm)" current=0.030 package="3 mm [THT]"]
  Keypad4x1 = Keypad Membran 4x4
  LCM1602_IIC1 = LCM1602 IIC [part_number="LCM1602 IIC" chip_label="LCM1602 IIC" package="DIP (Dual Inline) [THT]"]
  LCD2 = LCD screen [part_number=FFF]

nets:
  N1: Composant2.A0, LED1.cathode
  N2: Composant2.A1, LED2.cathode
  N3: Composant2.A2, LED3.cathode
  N4: Composant2.A4/SDA, LCM1602_IIC1.SDA
  N5: Composant2.A5/SCL, LCM1602_IIC1.SCL
  N6: Composant2.D8, Keypad4x1.Pin2
  N7: Composant2.D9_PWM, Keypad4x1.Pin1
  N8: Composant2.D10_PWM/SS, J1.pin2
  N9: Composant2.D2, Keypad4x1.Pin8
  N10: Composant2.D3_PWM, Keypad4x1.Pin7
  N11: Composant2.D4, Keypad4x1.Pin6
  N12: Composant2.D5_PWM, Keypad4x1.Pin5
  N13: Composant2.D6_PWM, Keypad4x1.Pin4
  N14: Composant2.D7, Keypad4x1.Pin3
  5V: Composant2.5V, LED1.anode, LED2.anode, LED3.anode, LCM1602_IIC1.VCC
  GND: Composant2.GND, J1.pin1, LCM1602_IIC1.GND
  VSS: LCM1602_IIC1.VSS, LCD2.VSS
  VDD: LCM1602_IIC1.VDD, LCD2.VDD
  N15: LCM1602_IIC1.V0, LCD2.V0
  N16: LCM1602_IIC1.RS, LCD2.RS
  N17: LCM1602_IIC1.RW, LCD2.R/W
  N18: LCM1602_IIC1.E, LCD2.E
  N19: LCM1602_IIC1.D0, LCD2.DB0
  N20: LCM1602_IIC1.D1, LCD2.DB1
  N21: LCM1602_IIC1.D2, LCD2.DB2
  N22: LCM1602_IIC1.D3, LCD2.DB3
  N23: LCM1602_IIC1.D4, LCD2.DB4
  N24: LCM1602_IIC1.D5, LCD2.DB5
  N25: LCM1602_IIC1.D6, LCD2.DB6
  N26: LCM1602_IIC1.D7, LCD2.DB7
  N27: LCM1602_IIC1.A, LCD2.LED+
  N28: LCM1602_IIC1.K, LCD2.LED-

custom parts:
  Keypad Membran 4x4: Membrane Keypad 4x4 Matrix
  LCM1602 IIC: I2C-Module to use a 1602 or 2004 LCD on with the wire.h libory Serial LCD Modul
